# Fritzing sketch HC-04 5led (saved by Fritzing 0.9.2b)
breadboards: 1

parts:
  Part1 = Arduino Uno (Rev3)
  R1 = Resistor [tolerance=±5% resistance=220 package=THT]
  R2 = Resistor [tolerance=±5% resistance=220 package=THT]
  R3 = Resistor [tolerance=±5% resistance=220 package=THT]
  R4 = Resistor [tolerance=±5% resistance=220 package=THT]
  R5 = Resistor [tolerance=±5% resistance=220 package=THT]
  LED1 = LED - 5mm [color="Green (570nm)" package="5 mm [THT]"]
  LED2 = LED - 5mm [color="Green (570nm)" package="5 mm [THT]"]
  LED3 = LED - 5mm [color="Yellow (595nm)" package="5 mm [THT]"]
  LED4 = LED - 5mm [color="Yellow (595nm)" package="5 mm [THT]"]
  LED5 = LED - 5mm [color="Red (660nm)" package="5 mm [THT]"]
  Part2 = SRF05 Ultrasonic Rangefinder

nets:
  N1: Part1.D8, LED4.anode
  N2: Part1.D9_PWM, LED3.anode
  N3: Part1.D10_PWM/SS, LED2.anode
  N4: Part1.D11_PWM/MOSI, LED1.anode
  N5: Part1.D12/MISO, Part2.Trig
  N6: Part1.D13/SCK, Part2.Echo
  N7: Part1.D7, LED5.anode
  5V: Part1.5V, Part2.VCC
  GND: Part1.GND, R1.Pin_1, R2.Pin_1, R3.Pin_1, R4.Pin_1, R5.Pin_1, Part2.GND
  N8: R1.Pin_0, LED1.cathode
  N9: R2.Pin_0, LED2.cathode
  N10: R3.Pin_0, LED3.cathode
  N11: R4.Pin_0, LED4.cathode
  N12: R5.Pin_0, LED5.cathode
