# Fritzing sketch gy-51 MPU6050 (saved by Fritzing 0.9.2b)
breadboards: 1

parts:
  Part1 = Arduino Nano (Rev3.0)
  GY1 = GY-521 (MPU-6050) [form="♀ (female)" package=THT]

nets:
  N1: Part1.GND, GY1.pin2
  N2: Part1.D2, GY1.pin8
  N3: Part1.5V, GY1.pin1
  N4: Part1.A5, GY1.pin3
  N5: Part1.A4, GY1.pin4

custom parts:
  GY-521 (MPU-6050): Placa GY-521 basada en conjunto de acelerómetro+giroscopios MPU-6050
