# Fritzing sketch bt_relay (saved by Fritzing 0.9.2b)

parts:
  Part1 = Bluetooth HC-06
  Part2 = Arduino Uno (Rev3)
  KY-1 = Keyes Relay [package=THT]

nets:
  N1: Part1.RXD, Part2.D7
  N2: Part1.TXD, Part2.D5_PWM
  GND: Part1.GND, Part2.GND, KY-1.ground
  VCC: Part1.VCC, Part2.3V3
  N3: Part2.D4, KY-1.signal
  N4: Part2.5V, KY-1.power

custom parts:
  Keyes Relay: The Keyes 5V relay module is suitable for SCM development, home appliance control. It uses a 5V~12V TIL control signal which can control DC / AC signal.
