# Fritzing sketch 7 segment (saved by Fritzing 0.9.2b)
breadboards: 1

parts:
  Part1 = Arduino Nano (Rev3.0)
  DI1 = 7-Segment LED Display [package=THT]

nets:
  N1: Part1.GND, DI1.commAnode#7
  N2: Part1.D2, DI1.cathodeB
  N3: Part1.D3, DI1.cathodeA
  N4: Part1.D4, DI1.cathodeC
  N5: Part1.D5, DI1.cathodeD
  N6: Part1.D6, DI1.cathodeE
  N7: Part1.D7, DI1.cathodeF
  N8: Part1.D8, DI1.cathodeG
