# Fritzing sketch mq135_alcohol_analyzer (saved by Fritzing 0.9.2b)
breadboards: 1

parts:
  MQ-135_Breakout1 = Gas Sensor Breakout Board
  LED1 = LED - 5mm [color="Orange (620nm)" package="5 mm [THT]"]
  LED2 = LED - 5mm [color="Red (633nm)" package="5 mm [THT]"]
  LED3 = LED - 5mm [color="Green (570nm)" package="5 mm [THT]"]
  Part1 = Arduino Uno (Rev3)

nets:
  GND: MQ-135_Breakout1.GND, LED1.cathode, LED2.cathode, LED3.cathode, Part1.GND
  N1: MQ-135_Breakout1.AOUT, Part1.A0
  5V: MQ-135_Breakout1.5V, Part1.5V
  N2: LED1.anode, Part1.D3_PWM
  N3: LED2.anode, Part1.D4
  N4: LED3.anode, Part1.D2

custom parts:
  Gas Sensor Breakout Board: Gas sensor breakout board. Input voltage is 5V. Sensor output is available in analog and digital.
