# Fritzing sketch czujka PIR (saved by Fritzing 0.9.2b)
breadboards: 1

parts:
  Part1 = Arduino Uno (Rev3)
  PIR1 = PIR sensor
  J1 = Piezo Speaker
  LED1 = RGB LED (com. anode, rbg) [package="5 mm [THT]"]

nets:
  N1: Part1.D10_PWM/SS, LED1.green_cathode
  N2: Part1.D11_PWM/MOSI, LED1.red_cathode
  N3: Part1.D12/MISO, J1.pin2
  GND: Part1.GND, PIR1.GND, J1.pin1, LED1.common_anode
  N4: Part1.D2, PIR1.SIG
  5V: Part1.5V, PIR1.VDD
