# Fritzing sketch Nokia-5110-DHT11 (saved by Fritzing 0.9.2b)
breadboards: 1

parts:
  Part1 = Arduino Nano (Rev3.0)
  DHT1 = DHT11 Humitidy and Temperature Sensor
  GLCD_84x1 = 84 x 48 Graphic LCD

nets:
  GND: Part1.GND, DHT1.GND, GLCD_84x1.8_GND
  N1: Part1.D7, DHT1.DATA
  N2: Part1.D8, GLCD_84x1.5_CLK
  N3: Part1.D9, GLCD_84x1.4_DIN
  N4: Part1.D10, GLCD_84x1.3_DC
  N5: Part1.D11/MOSI, GLCD_84x1.1_RST
  N6: Part1.D12/MISO, GLCD_84x1.2_CE
  N7: Part1.VIN, GLCD_84x1.6_VCC
  5V: Part1.5V, DHT1.VDD
  N8: Part1.3V3, GLCD_84x1.7_LIGHT

custom parts:
  DHT11 Humitidy and Temperature Sensor: DHT11 Humidity and Temperature Sensor
